// Logisim project hack_architecture_CPU.circ as structural Verilog
module main (
);

  Program_Counter program_counter_1 ();  // open: In, Inc, Load, Reset, Clk, out_6
  _256Kb_Ram u_256kb_ram_1 ();  // open: Addr_14_bits, Data, Load, Clk, out_5
  ALU alu_1 ();  // open: x, y, Output_8bits, zr, ng, zx, zy, nx, ny, f, no
endmodule

module ALU (
  input  zx,
  input  zy,
  input  nx,
  input  ny,
  input  f,
  input  no,
  input  [15:0] x,
  input  [15:0] y,
  output [15:0] Output_8bits,
  output zr,
  output ng
);

  wire [15:0] adder_1_out, and_1_out, multiplexer_16_bits_1_out_4, multiplexer_16_bits_2_out_4,
       multiplexer_16_bits_3_out_4, multiplexer_16_bits_4_out_4, multiplexer_16_bits_5_out_4, not_1_out,
       not_2_out, not_3_out;

  Multiplexer_16_bits multiplexer_16_bits_1 (.A(x), .B({16{1'b0}}), .Select(zx), .out_4(multiplexer_16_bits_1_out_4));
  assign not_1_out = ~multiplexer_16_bits_1_out_4;  // NOT_Gate not_1, 16 bits wide
  Multiplexer_16_bits multiplexer_16_bits_2 (.A(y), .B({16{1'b0}}), .Select(zy), .out_4(multiplexer_16_bits_2_out_4));
  assign not_2_out = ~multiplexer_16_bits_2_out_4;  // NOT_Gate not_2, 16 bits wide
  Multiplexer_16_bits multiplexer_16_bits_3 (
    .A(multiplexer_16_bits_1_out_4), .B(not_1_out), .Select(nx), .out_4(multiplexer_16_bits_3_out_4));
  Multiplexer_16_bits multiplexer_16_bits_4 (
    .A(multiplexer_16_bits_2_out_4), .B(not_2_out), .Select(ny), .out_4(multiplexer_16_bits_4_out_4));
  assign and_1_out = multiplexer_16_bits_3_out_4 & multiplexer_16_bits_4_out_4;  // AND_Gate and_1, 16 bits wide
  Adder #(.width(16)) adder_1 (
    .a(multiplexer_16_bits_3_out_4), .b(multiplexer_16_bits_4_out_4), .out(adder_1_out), .cin(1'b0));  // open: cout
  Multiplexer_16_bits multiplexer_16_bits_5 (
    .A(and_1_out), .B(adder_1_out), .Select(f), .out_4(multiplexer_16_bits_5_out_4));
  assign not_3_out = ~multiplexer_16_bits_5_out_4;  // NOT_Gate not_3, 16 bits wide
  Multiplexer_16_bits multiplexer_16_bits_6 (
    .A(multiplexer_16_bits_5_out_4), .B(not_3_out), .Select(no), .out_4(Output_8bits));
  nand nand_1 (zr, Output_8bits[0], Output_8bits[1], Output_8bits[2], Output_8bits[3], Output_8bits[4], Output_8bits[5], Output_8bits[6], Output_8bits[7], Output_8bits[8], Output_8bits[9], Output_8bits[10], Output_8bits[11], Output_8bits[12], Output_8bits[13], Output_8bits[14], Output_8bits[15]);
  buf buffer_1 (ng, Output_8bits[15]);
endmodule

module Multiplexer_16_bits (
  input  [15:0] A,
  input  [15:0] B,
  input  Select,
  output [15:0] out_4
);

  wire [15:0] and_1_out, and_2_out, not_1_out;

  assign not_1_out = ~{16{Select}};  // NOT_Gate not_1, 16 bits wide
  assign and_1_out = A & not_1_out;  // AND_Gate and_1, 16 bits wide
  assign and_2_out = {16{Select}} & B;  // AND_Gate and_2, 16 bits wide
  assign out_4 = and_1_out | and_2_out;  // OR_Gate or_1, 16 bits wide

  // Other names for the same wires on the sheet: sel[15:0] = {16{Select}}
endmodule

module _1_bit_register (
  input  In,
  input  Load,
  input  Clk,
  output out_4
);

  wire multiplexer_1_out;

  Multiplexer multiplexer_1 (.in0(out_4), .in1(In), .out(multiplexer_1_out), .sel(Load));  // open: en
  D_Flip_Flop d_ff_1 (.clk(Clk), .D(multiplexer_1_out), .Q(out_4));  // open: Qn, preset, en, reset
endmodule

module _16_bits_register (
  input  [15:0] in_1,
  input  Load,
  input  Clk,
  output [15:0] out_4,
  output [3:0] out_5
);

  _1_bit_register u_1_bit_register_1 (.In(in_1[0]), .out_4(out_4[0]), .Load(Load), .Clk(Clk));
  _1_bit_register u_1_bit_register_2 (.In(in_1[1]), .out_4(out_4[1]), .Load(Load), .Clk(Clk));
  _1_bit_register u_1_bit_register_3 (.In(in_1[2]), .out_4(out_4[2]), .Load(Load), .Clk(Clk));
  _1_bit_register u_1_bit_register_4 (.In(in_1[3]), .out_4(out_4[3]), .Load(Load), .Clk(Clk));
  _1_bit_register u_1_bit_register_5 (.In(in_1[4]), .out_4(out_4[4]), .Load(Load), .Clk(Clk));
  _1_bit_register u_1_bit_register_6 (.In(in_1[5]), .out_4(out_4[5]), .Load(Load), .Clk(Clk));
  _1_bit_register u_1_bit_register_7 (.In(in_1[6]), .out_4(out_4[6]), .Load(Load), .Clk(Clk));
  _1_bit_register u_1_bit_register_8 (.In(in_1[7]), .out_4(out_4[7]), .Load(Load), .Clk(Clk));
  _1_bit_register u_1_bit_register_9 (.In(in_1[8]), .out_4(out_4[8]), .Load(Load), .Clk(Clk));
  _1_bit_register u_1_bit_register_10 (.In(in_1[9]), .out_4(out_4[9]), .Load(Load), .Clk(Clk));
  _1_bit_register u_1_bit_register_11 (.In(in_1[10]), .out_4(out_4[10]), .Load(Load), .Clk(Clk));
  _1_bit_register u_1_bit_register_12 (.In(in_1[11]), .out_4(out_4[11]), .Load(Load), .Clk(Clk));
  _1_bit_register u_1_bit_register_13 (.In(in_1[12]), .out_4(out_4[12]), .Load(Load), .Clk(Clk));
  _1_bit_register u_1_bit_register_14 (.In(in_1[13]), .out_4(out_4[13]), .Load(Load), .Clk(Clk));
  _1_bit_register u_1_bit_register_15 (.In(in_1[14]), .out_4(out_4[14]), .Load(Load), .Clk(Clk));
  _1_bit_register u_1_bit_register_16 (.In(in_1[15]), .out_4(out_4[15]), .Load(Load), .Clk(Clk));

  assign out_5 = out_4[3:0];
endmodule

module Dmux8ways16bits (
  input  [2:0] Sel,
  input  [15:0] in_2,
  output [15:0] out_3,
  output [15:0] out_4,
  output [15:0] out_5,
  output [15:0] out_6,
  output [15:0] out_7,
  output [15:0] out_8,
  output [15:0] out_9,
  output [15:0] out_10
);

  wire [15:0] and_1_out, and_2_out, and_3_out, and_4_out, and_5_out, and_6_out, and_7_out, and_8_out,
       and_9_out, and_10_out, and_11_out, and_12_out, and_13_out, and_14_out, and_15_out, and_16_out,
       not_1_out, not_2_out, not_3_out;

  assign not_1_out = ~{16{Sel[2]}};  // NOT_Gate not_1, 16 bits wide
  assign not_2_out = ~{16{Sel[1]}};  // NOT_Gate not_2, 16 bits wide
  assign not_3_out = ~{16{Sel[0]}};  // NOT_Gate not_3, 16 bits wide
  assign and_1_out = in_2 & not_2_out;  // AND_Gate and_1, 16 bits wide
  assign and_2_out = in_2 & not_2_out;  // AND_Gate and_2, 16 bits wide
  assign and_3_out = in_2 & {16{Sel[1]}};  // AND_Gate and_3, 16 bits wide
  assign and_4_out = in_2 & not_1_out;  // AND_Gate and_4, 16 bits wide
  assign and_5_out = in_2 & {16{Sel[2]}};  // AND_Gate and_5, 16 bits wide
  assign and_6_out = in_2 & {16{Sel[2]}};  // AND_Gate and_6, 16 bits wide
  assign and_7_out = in_2 & {16{Sel[2]}};  // AND_Gate and_7, 16 bits wide
  assign and_8_out = in_2 & {16{Sel[2]}};  // AND_Gate and_8, 16 bits wide
  assign and_9_out = and_1_out & not_1_out;  // AND_Gate and_9, 16 bits wide
  assign and_10_out = and_2_out & not_1_out;  // AND_Gate and_10, 16 bits wide
  assign and_11_out = and_3_out & not_1_out;  // AND_Gate and_11, 16 bits wide
  assign and_12_out = and_4_out & {16{Sel[1]}};  // AND_Gate and_12, 16 bits wide
  assign and_13_out = and_5_out & not_2_out;  // AND_Gate and_13, 16 bits wide
  assign and_14_out = and_6_out & not_2_out;  // AND_Gate and_14, 16 bits wide
  assign and_15_out = and_7_out & {16{Sel[1]}};  // AND_Gate and_15, 16 bits wide
  assign and_16_out = and_8_out & {16{Sel[1]}};  // AND_Gate and_16, 16 bits wide
  assign out_3 = and_9_out & not_3_out;  // AND_Gate and_17, 16 bits wide
  assign out_4 = and_10_out & {16{Sel[0]}};  // AND_Gate and_18, 16 bits wide
  assign out_5 = and_11_out & not_3_out;  // AND_Gate and_19, 16 bits wide
  assign out_6 = and_12_out & {16{Sel[0]}};  // AND_Gate and_20, 16 bits wide
  assign out_7 = and_13_out & not_3_out;  // AND_Gate and_21, 16 bits wide
  assign out_8 = and_14_out & {16{Sel[0]}};  // AND_Gate and_22, 16 bits wide
  assign out_9 = and_15_out & not_3_out;  // AND_Gate and_23, 16 bits wide
  assign out_10 = and_16_out & {16{Sel[0]}};  // AND_Gate and_24, 16 bits wide

  // Other names for the same wires on the sheet: sel0_16[15:0] = {16{Sel[0]}}; sel1_16[15:0] = {16{Sel[1]}};
  //   sel2_16[15:0] = {16{Sel[2]}}
endmodule

module Mux8ways16bits (
  input  [15:0] in_1,
  input  [2:0] Sel,
  input  [15:0] in_3,
  input  [15:0] in_4,
  input  [15:0] in_5,
  input  [15:0] in_6,
  input  [15:0] in_7,
  input  [15:0] in_8,
  input  [15:0] in_9,
  output [15:0] out_10
);

  wire [15:0] and_1_out, and_2_out, and_3_out, and_4_out, and_5_out, and_6_out, and_7_out, and_8_out,
       not_1_out, not_2_out, not_3_out, or_1_out, or_2_out, or_3_out, or_4_out, or_5_out, or_6_out;

  assign not_1_out = ~{16{Sel[2]}};  // NOT_Gate not_1, 16 bits wide
  assign not_2_out = ~{16{Sel[1]}};  // NOT_Gate not_2, 16 bits wide
  assign not_3_out = ~{16{Sel[0]}};  // NOT_Gate not_3, 16 bits wide
  assign and_1_out = in_1 & not_1_out & not_2_out & not_3_out;  // AND_Gate and_1, 16 bits wide
  assign and_2_out = in_3 & not_1_out & not_2_out & {16{Sel[0]}};  // AND_Gate and_2, 16 bits wide
  assign and_3_out = in_4 & not_1_out & {16{Sel[1]}} & not_3_out;  // AND_Gate and_3, 16 bits wide
  assign and_4_out = in_5 & not_1_out & {16{Sel[1]}} & {16{Sel[0]}};  // AND_Gate and_4, 16 bits wide
  assign and_5_out = in_6 & {16{Sel[2]}} & not_2_out & not_3_out;  // AND_Gate and_5, 16 bits wide
  assign and_6_out = in_7 & {16{Sel[2]}} & not_2_out & {16{Sel[0]}};  // AND_Gate and_6, 16 bits wide
  assign and_7_out = in_8 & {16{Sel[2]}} & {16{Sel[1]}} & not_3_out;  // AND_Gate and_7, 16 bits wide
  assign and_8_out = in_9 & {16{Sel[2]}} & {16{Sel[1]}} & {16{Sel[0]}};  // AND_Gate and_8, 16 bits wide
  assign or_1_out = and_1_out | and_2_out;  // OR_Gate or_1, 16 bits wide
  assign or_2_out = and_3_out | and_4_out;  // OR_Gate or_2, 16 bits wide
  assign or_3_out = and_5_out | and_6_out;  // OR_Gate or_3, 16 bits wide
  assign or_4_out = and_7_out | and_8_out;  // OR_Gate or_4, 16 bits wide
  assign or_5_out = or_1_out | or_2_out;  // OR_Gate or_5, 16 bits wide
  assign or_6_out = or_3_out | or_4_out;  // OR_Gate or_6, 16 bits wide
  assign out_10 = or_5_out | or_6_out;  // OR_Gate or_7, 16 bits wide

  // Other names for the same wires on the sheet: sel0_16[15:0] = {16{Sel[0]}}; sel1_16[15:0] = {16{Sel[1]}};
  //   sel2_16[15:0] = {16{Sel[2]}}
endmodule

module _128_bits_Ram (
  input  [15:0] In,
  input  [2:0] Addr,
  input  Load,
  input  Clk,
  output [15:0] out_5
);

  wire loadR1, loadR2, loadR3, loadR4, loadR5, loadR6, loadR7, loadR8;
  wire [3:0] n16_bits_register_1_out_5, n16_bits_register_2_out_5, n16_bits_register_3_out_5,
       n16_bits_register_4_out_5, n16_bits_register_5_out_5, n16_bits_register_6_out_5,
       n16_bits_register_7_out_5, n16_bits_register_8_out_5;
  wire [15:0] dmux8ways16bits_1_out_3, dmux8ways16bits_1_out_4, dmux8ways16bits_1_out_5,
       dmux8ways16bits_1_out_6, dmux8ways16bits_1_out_7, dmux8ways16bits_1_out_8, dmux8ways16bits_1_out_9,
       dmux8ways16bits_1_out_10, n16_bits_register_1_out_4, n16_bits_register_2_out_4,
       n16_bits_register_3_out_4, n16_bits_register_4_out_4, n16_bits_register_5_out_4,
       n16_bits_register_6_out_4, n16_bits_register_7_out_4, n16_bits_register_8_out_4;

  Dmux8ways16bits dmux8ways16bits_1 (
    .Sel(Addr), .in_2(In), .out_3(dmux8ways16bits_1_out_3), .out_4(dmux8ways16bits_1_out_4),
    .out_5(dmux8ways16bits_1_out_5), .out_6(dmux8ways16bits_1_out_6), .out_7(dmux8ways16bits_1_out_7),
    .out_8(dmux8ways16bits_1_out_8), .out_9(dmux8ways16bits_1_out_9), .out_10(dmux8ways16bits_1_out_10));
  Demultiplexer #(.select(3), .enable("false")) demultiplexer_1 (
    .out0(loadR1), .out1(loadR2), .out2(loadR3), .out3(loadR4), .out4(loadR5), .out5(loadR6), .out6(loadR7),
    .out7(loadR8), .in(Load), .sel(Addr));
  Hex_Digit_Display hex_digit_display_1 (.value(n16_bits_register_1_out_5));  // open: dp
  _16_bits_register u_16_bits_register_1 (
    .in_1(dmux8ways16bits_1_out_3), .out_4(n16_bits_register_1_out_4), .Load(loadR1), .Clk(Clk),
    .out_5(n16_bits_register_1_out_5));
  _16_bits_register u_16_bits_register_2 (
    .in_1(dmux8ways16bits_1_out_4), .out_4(n16_bits_register_2_out_4), .Load(loadR2), .Clk(Clk),
    .out_5(n16_bits_register_2_out_5));
  _16_bits_register u_16_bits_register_3 (
    .in_1(dmux8ways16bits_1_out_5), .out_4(n16_bits_register_3_out_4), .Load(loadR3), .Clk(Clk),
    .out_5(n16_bits_register_3_out_5));
  _16_bits_register u_16_bits_register_4 (
    .in_1(dmux8ways16bits_1_out_6), .out_4(n16_bits_register_4_out_4), .Load(loadR4), .Clk(Clk),
    .out_5(n16_bits_register_4_out_5));
  _16_bits_register u_16_bits_register_5 (
    .in_1(dmux8ways16bits_1_out_7), .out_4(n16_bits_register_5_out_4), .Load(loadR5), .Clk(Clk),
    .out_5(n16_bits_register_5_out_5));
  _16_bits_register u_16_bits_register_6 (
    .in_1(dmux8ways16bits_1_out_8), .out_4(n16_bits_register_6_out_4), .Load(loadR6), .Clk(Clk),
    .out_5(n16_bits_register_6_out_5));
  _16_bits_register u_16_bits_register_7 (
    .in_1(dmux8ways16bits_1_out_9), .out_4(n16_bits_register_7_out_4), .Load(loadR7), .Clk(Clk),
    .out_5(n16_bits_register_7_out_5));
  _16_bits_register u_16_bits_register_8 (
    .in_1(dmux8ways16bits_1_out_10), .out_4(n16_bits_register_8_out_4), .Load(loadR8), .Clk(Clk),
    .out_5(n16_bits_register_8_out_5));
  Hex_Digit_Display hex_digit_display_2 (.value(n16_bits_register_2_out_5));  // open: dp
  Hex_Digit_Display hex_digit_display_3 (.value(n16_bits_register_3_out_5));  // open: dp
  Hex_Digit_Display hex_digit_display_4 (.value(n16_bits_register_4_out_5));  // open: dp
  Hex_Digit_Display hex_digit_display_5 (.value(n16_bits_register_5_out_5));  // open: dp
  Hex_Digit_Display hex_digit_display_6 (.value(n16_bits_register_6_out_5));  // open: dp
  Hex_Digit_Display hex_digit_display_7 (.value(n16_bits_register_7_out_5));  // open: dp
  Hex_Digit_Display hex_digit_display_8 (.value(n16_bits_register_8_out_5));  // open: dp
  Mux8ways16bits mux8ways16bits_1 (
    .in_1(n16_bits_register_1_out_4), .Sel(Addr), .in_3(n16_bits_register_2_out_4),
    .in_4(n16_bits_register_3_out_4), .in_5(n16_bits_register_4_out_4), .in_6(n16_bits_register_5_out_4),
    .in_7(n16_bits_register_6_out_4), .in_8(n16_bits_register_7_out_4), .in_9(n16_bits_register_8_out_4),
    .out_10(out_5));
endmodule

module _1024_bits_Ram (
  input  [5:0] Addr,
  input  Load,
  input  [15:0] Data,
  input  Clk,
  output [15:0] out_5
);

  wire Load0, Load1, Load2, Load3, Load4, Load5, Load6, Load7, not_1_out, not_2_out, not_3_out, not_4_out,
       not_5_out, not_6_out, not_7_out, not_8_out;
  wire [2:0] Addr_3_t;
  wire [5:0] demultiplexer_3_out0, demultiplexer_3_out1, demultiplexer_3_out2, demultiplexer_3_out3,
       demultiplexer_3_out4, demultiplexer_3_out5, demultiplexer_3_out6, demultiplexer_3_out7;
  wire [15:0] controlled_buffer_1_out, controlled_buffer_2_out, controlled_buffer_3_out,
       controlled_buffer_4_out, controlled_buffer_5_out, controlled_buffer_6_out, controlled_buffer_7_out,
       controlled_buffer_8_out, Data0, Data1, Data2, Data3, Data4, Data5, Data6, Data7;

  Demultiplexer #(.select(3), .enable("false")) demultiplexer_1 (
    .out0(Load0), .out1(Load1), .out2(Load2), .out3(Load3), .out4(Load4), .out5(Load5), .out6(Load6),
    .out7(Load7), .in(Load), .sel(Addr[5:3]));
  Demultiplexer #(.select(3), .width(16), .enable("false")) demultiplexer_2 (
    .out0(Data0), .out1(Data1), .out2(Data2), .out3(Data3), .out4(Data4), .out5(Data5), .out6(Data6),
    .out7(Data7), .in(Data), .sel(Addr[5:3]));
  Demultiplexer #(.select(3), .width(6), .enable("false")) demultiplexer_3 (
    .out0(demultiplexer_3_out0), .out1(demultiplexer_3_out1), .out2(demultiplexer_3_out2),
    .out3(demultiplexer_3_out3), .out4(demultiplexer_3_out4), .out5(demultiplexer_3_out5),
    .out6(demultiplexer_3_out6), .out7(demultiplexer_3_out7), .in(Addr), .sel(Addr_3_t));
  assign controlled_buffer_1_out = Load0 ? Data0 : 16'bz;  // Controlled_Buffer controlled_buffer_1
  not not_1 (not_1_out, Load0);
  assign controlled_buffer_2_out = Load1 ? Data1 : 16'bz;  // Controlled_Buffer controlled_buffer_2
  not not_2 (not_2_out, Load1);
  assign controlled_buffer_3_out = Load2 ? Data2 : 16'bz;  // Controlled_Buffer controlled_buffer_3
  not not_3 (not_3_out, Load2);
  assign controlled_buffer_4_out = Load3 ? Data3 : 16'bz;  // Controlled_Buffer controlled_buffer_4
  not not_4 (not_4_out, Load3);
  assign controlled_buffer_5_out = Load4 ? Data4 : 16'bz;  // Controlled_Buffer controlled_buffer_5
  not not_5 (not_5_out, Load4);
  assign controlled_buffer_6_out = Load5 ? Data5 : 16'bz;  // Controlled_Buffer controlled_buffer_6
  not not_6 (not_6_out, Load5);
  assign controlled_buffer_7_out = Load6 ? Data6 : 16'bz;  // Controlled_Buffer controlled_buffer_7
  not not_7 (not_7_out, Load6);
  assign controlled_buffer_8_out = Load7 ? Data7 : 16'bz;  // Controlled_Buffer controlled_buffer_8
  not not_8 (not_8_out, Load7);
  RAM #(.addrWidth(6), .dataWidth(16)) ram_1 (
    .addr(demultiplexer_3_out0), .data(controlled_buffer_1_out), .clk(Clk), .ld(not_1_out));  // open: sel, clr
  RAM #(.addrWidth(6), .dataWidth(16)) ram_2 (
    .addr(demultiplexer_3_out1), .data(controlled_buffer_2_out), .clk(Clk), .ld(not_2_out));  // open: sel, clr
  RAM #(.addrWidth(6), .dataWidth(16)) ram_3 (
    .addr(demultiplexer_3_out2), .data(controlled_buffer_3_out), .clk(Clk), .ld(not_3_out));  // open: sel, clr
  RAM #(.addrWidth(6), .dataWidth(16)) ram_4 (
    .addr(demultiplexer_3_out3), .data(controlled_buffer_4_out), .clk(Clk), .ld(not_4_out));  // open: sel, clr
  RAM #(.addrWidth(6), .dataWidth(16)) ram_5 (
    .addr(demultiplexer_3_out4), .data(controlled_buffer_5_out), .clk(Clk), .ld(not_5_out));  // open: sel, clr
  RAM #(.addrWidth(6), .dataWidth(16)) ram_6 (
    .addr(demultiplexer_3_out5), .data(controlled_buffer_6_out), .clk(Clk), .ld(not_6_out));  // open: sel, clr
  RAM #(.addrWidth(6), .dataWidth(16)) ram_7 (
    .addr(demultiplexer_3_out6), .data(controlled_buffer_7_out), .clk(Clk), .ld(not_7_out));  // open: sel, clr
  RAM #(.addrWidth(6), .dataWidth(16)) ram_8 (
    .addr(demultiplexer_3_out7), .data(controlled_buffer_8_out), .clk(Clk), .ld(not_8_out));  // open: sel, clr
  Multiplexer #(.select(3), .width(16), .enable("false")) multiplexer_1 (
    .in0(controlled_buffer_1_out), .in1(controlled_buffer_2_out), .in2(controlled_buffer_3_out),
    .in3(controlled_buffer_4_out), .in4(controlled_buffer_5_out), .in5(controlled_buffer_6_out),
    .in6(controlled_buffer_7_out), .in7(controlled_buffer_8_out), .out(out_5), .sel(Addr[5:3]));

  // Other names for the same wires on the sheet: Addr_3[2:0] = Addr[5:3]
endmodule

module _256Kb_Ram (
  input  [13:0] Addr_14_bits,
  input  [15:0] Data,
  input  Load,
  input  Clk,
  output [15:0] out_5
);

  wire not_1_out;

  assign out_5 = Load ? Data : 16'bz;  // Controlled_Buffer controlled_buffer_1
  not not_1 (not_1_out, Load);
  RAM #(.addrWidth(14), .dataWidth(16)) ram_1 (
    .addr(Addr_14_bits), .data(out_5), .clk(Clk), .ld(not_1_out));  // open: sel, clr
endmodule

module _16_bits_counter (
  input  Clk,
  input  Reset,
  output [15:0] out_3
);

  wire and_1_out, d_ff_1_qn, d_ff_2_qn, d_ff_3_qn, d_ff_4_qn, d_ff_5_qn, d_ff_6_qn, d_ff_7_qn, d_ff_8_qn,
       d_ff_9_qn, d_ff_10_qn, d_ff_11_qn, d_ff_12_qn, d_ff_13_qn, d_ff_14_qn, d_ff_15_qn, d_ff_16_qn;

  and and_1 (and_1_out, Clk, Reset);
  D_Flip_Flop d_ff_1 (.clk(Clk), .D(d_ff_1_qn), .Q(out_3[0]), .Qn(d_ff_1_qn), .reset(and_1_out));  // open: preset, en
  D_Flip_Flop d_ff_2 (
    .clk(d_ff_15_qn), .D(d_ff_2_qn), .Q(out_3[8]), .Qn(d_ff_2_qn), .reset(and_1_out));  // open: preset, en
  D_Flip_Flop d_ff_3 (
    .clk(d_ff_1_qn), .D(d_ff_3_qn), .Q(out_3[1]), .Qn(d_ff_3_qn), .reset(and_1_out));  // open: preset, en
  D_Flip_Flop d_ff_4 (
    .clk(d_ff_2_qn), .D(d_ff_4_qn), .Q(out_3[9]), .Qn(d_ff_4_qn), .reset(and_1_out));  // open: preset, en
  D_Flip_Flop d_ff_5 (
    .clk(d_ff_3_qn), .D(d_ff_5_qn), .Q(out_3[2]), .Qn(d_ff_5_qn), .reset(and_1_out));  // open: preset, en
  D_Flip_Flop d_ff_6 (
    .clk(d_ff_4_qn), .D(d_ff_6_qn), .Q(out_3[10]), .Qn(d_ff_6_qn), .reset(and_1_out));  // open: preset, en
  D_Flip_Flop d_ff_7 (
    .clk(d_ff_5_qn), .D(d_ff_7_qn), .Q(out_3[3]), .Qn(d_ff_7_qn), .reset(and_1_out));  // open: preset, en
  D_Flip_Flop d_ff_8 (
    .clk(d_ff_6_qn), .D(d_ff_8_qn), .Q(out_3[11]), .Qn(d_ff_8_qn), .reset(and_1_out));  // open: preset, en
  D_Flip_Flop d_ff_9 (
    .clk(d_ff_7_qn), .D(d_ff_9_qn), .Q(out_3[4]), .Qn(d_ff_9_qn), .reset(and_1_out));  // open: preset, en
  D_Flip_Flop d_ff_10 (
    .clk(d_ff_8_qn), .D(d_ff_10_qn), .Q(out_3[12]), .Qn(d_ff_10_qn), .reset(and_1_out));  // open: preset, en
  D_Flip_Flop d_ff_11 (
    .clk(d_ff_9_qn), .D(d_ff_11_qn), .Q(out_3[5]), .Qn(d_ff_11_qn), .reset(and_1_out));  // open: preset, en
  D_Flip_Flop d_ff_12 (
    .clk(d_ff_10_qn), .D(d_ff_12_qn), .Q(out_3[13]), .Qn(d_ff_12_qn), .reset(and_1_out));  // open: preset, en
  D_Flip_Flop d_ff_13 (
    .clk(d_ff_11_qn), .D(d_ff_13_qn), .Q(out_3[6]), .Qn(d_ff_13_qn), .reset(and_1_out));  // open: preset, en
  D_Flip_Flop d_ff_14 (
    .clk(d_ff_12_qn), .D(d_ff_14_qn), .Q(out_3[14]), .Qn(d_ff_14_qn), .reset(and_1_out));  // open: preset, en
  D_Flip_Flop d_ff_15 (
    .clk(d_ff_13_qn), .D(d_ff_15_qn), .Q(out_3[7]), .Qn(d_ff_15_qn), .reset(and_1_out));  // open: preset, en
  D_Flip_Flop d_ff_16 (
    .clk(d_ff_14_qn), .D(d_ff_16_qn), .Q(out_3[15]), .Qn(d_ff_16_qn), .reset(and_1_out));  // open: preset, en
endmodule

module Increment_16_bits (
  input  [15:0] in_1,
  output [15:0] out_2
);

  wire adder_1_cout, adder_2_cout, adder_3_cout, adder_4_cout, adder_5_cout, adder_6_cout, adder_7_cout,
       adder_8_cout, adder_9_cout, adder_10_cout, adder_11_cout, adder_12_cout, adder_13_cout, adder_14_cout,
       adder_15_cout;

  Adder #(.width(1)) adder_1 (.a(in_1[0]), .b(1'b1), .out(out_2[0]), .cout(adder_1_cout));  // open: cin
  Adder #(.width(1)) adder_2 (.a(in_1[1]), .b(1'b0), .out(out_2[1]), .cin(adder_1_cout), .cout(adder_2_cout));
  Adder #(.width(1)) adder_3 (.a(in_1[2]), .b(1'b0), .out(out_2[2]), .cin(adder_2_cout), .cout(adder_3_cout));
  Adder #(.width(1)) adder_4 (.a(in_1[3]), .b(1'b0), .out(out_2[3]), .cin(adder_3_cout), .cout(adder_4_cout));
  Adder #(.width(1)) adder_5 (.a(in_1[4]), .b(1'b0), .out(out_2[4]), .cin(adder_4_cout), .cout(adder_5_cout));
  Adder #(.width(1)) adder_6 (.a(in_1[5]), .b(1'b0), .out(out_2[5]), .cin(adder_5_cout), .cout(adder_6_cout));
  Adder #(.width(1)) adder_7 (.a(in_1[6]), .b(1'b0), .out(out_2[6]), .cin(adder_6_cout), .cout(adder_7_cout));
  Adder #(.width(1)) adder_8 (.a(in_1[7]), .b(1'b0), .out(out_2[7]), .cin(adder_7_cout), .cout(adder_8_cout));
  Adder #(.width(1)) adder_9 (.a(in_1[8]), .b(1'b0), .out(out_2[8]), .cin(adder_8_cout), .cout(adder_9_cout));
  Adder #(.width(1)) adder_10 (.a(in_1[9]), .b(1'b0), .out(out_2[9]), .cin(adder_9_cout), .cout(adder_10_cout));
  Adder #(.width(1)) adder_11 (.a(in_1[10]), .b(1'b0), .out(out_2[10]), .cin(adder_10_cout), .cout(adder_11_cout));
  Adder #(.width(1)) adder_12 (.a(in_1[11]), .b(1'b0), .out(out_2[11]), .cin(adder_11_cout), .cout(adder_12_cout));
  Adder #(.width(1)) adder_13 (.a(in_1[12]), .b(1'b0), .out(out_2[12]), .cin(adder_12_cout), .cout(adder_13_cout));
  Adder #(.width(1)) adder_14 (.a(in_1[13]), .b(1'b0), .out(out_2[13]), .cin(adder_13_cout), .cout(adder_14_cout));
  Adder #(.width(1)) adder_15 (.a(in_1[14]), .b(1'b0), .out(out_2[14]), .cin(adder_14_cout), .cout(adder_15_cout));
  Adder #(.width(1)) adder_16 (.a(in_1[15]), .b(1'b0), .out(out_2[15]), .cin(adder_15_cout));  // open: cout
endmodule

module Program_Counter (
  input  [15:0] In,
  input  Inc,
  input  Load,
  input  Reset,
  input  Clk,
  output [15:0] out_6
);

  wire [3:0] n16_bits_register_1_out_5;
  wire [15:0] buffer_1_out, increment_16_bits_1_out_2, multiplexer_1_out, multiplexer_2_out,
       multiplexer_3_out;

  assign buffer_1_out = out_6;  // Buffer buffer_1, 16 bits wide
  Increment_16_bits increment_16_bits_1 (.out_2(increment_16_bits_1_out_2), .in_1(buffer_1_out));
  Multiplexer #(.width(16), .enable("false")) multiplexer_1 (
    .in0(buffer_1_out), .in1(increment_16_bits_1_out_2), .out(multiplexer_1_out), .sel(Inc));
  Multiplexer #(.width(16), .enable("false")) multiplexer_2 (
    .in0(multiplexer_1_out), .in1(In), .out(multiplexer_2_out), .sel(Load));
  Multiplexer #(.width(16), .enable("false")) multiplexer_3 (
    .in0(multiplexer_2_out), .in1({16{1'b0}}), .out(multiplexer_3_out), .sel(Reset));
  _16_bits_register u_16_bits_register_1 (
    .in_1(multiplexer_3_out), .out_4(out_6), .Load(1'b1), .Clk(Clk), .out_5(n16_bits_register_1_out_5));
  Hex_Digit_Display hex_digit_display_1 (.value(n16_bits_register_1_out_5));  // open: dp
endmodule

module Memmory (
  input  [15:0] In,
  input  [14:0] Addr,
  input  Load,
  input  in_4
);

  wire demultiplexer_1_out0, demultiplexer_1_out1;

  Demultiplexer #(.enable("false")) demultiplexer_1 (
    .out0(demultiplexer_1_out0), .out1(demultiplexer_1_out1), .in(Load), .sel(Addr[14]));
  _256Kb_Ram u_256kb_ram_1 (
    .Addr_14_bits(Addr[13:0]), .Data(In), .Load(demultiplexer_1_out0), .Clk(in_4));  // open: out_5

  // Notes on the sheet:
  //   Ram
  //   Screen
endmodule

module CPU (
  input  [15:0] Insturction,
  input  [15:0] InM,
  input  Reset,
  output [15:0] outM,
  output [15:0] outA,
  output [15:0] outD,
  output [14:0] PC,
  output writeM
);

  wire and_1_out, and_2_out, and_3_out, and_4_out, and_5_out, and_6_out, and_7_out, and_8_out, Clk, Ng,
       not_1_out, not_2_out, not_3_out, or_1_out, or_2_out, or_3_out, Zr;
  wire [15:0] multiplexer_1_out, multiplexer_2_out;
  wire [15:15] program_counter_1_out_6;

  Clock u_Clk (.out(Clk));
  not not_1 (not_1_out, Ng);
  and and_1 (and_1_out, Insturction[0], Insturction[15]);
  and and_2 (and_2_out, Insturction[1], Insturction[15]);
  and and_3 (and_3_out, Insturction[2], Insturction[15]);
  Multiplexer #(.width(16), .enable("false")) multiplexer_1 (
    .in0(Insturction), .in1(outM), .out(multiplexer_1_out), .sel(Insturction[15]));
  and and_4 (and_4_out, Insturction[5], Insturction[15]);
  not not_2 (not_2_out, Insturction[15]);
  and and_5 (and_5_out, Insturction[4], Insturction[15]);
  and and_6 (and_6_out, not_1_out, and_1_out);
  and and_7 (and_7_out, Zr, and_2_out);
  and and_8 (and_8_out, Ng, and_3_out);
  or or_1 (or_1_out, and_4_out, not_2_out);
  _16_bits_register u_16_bits_register_1 (.in_1(outM), .out_4(outD), .Load(and_5_out), .Clk(Clk));  // open: out_5
  or or_2 (or_2_out, and_6_out, and_7_out);
  or or_3 (or_3_out, or_2_out, and_8_out);
  _16_bits_register u_16_bits_register_2 (
    .in_1(multiplexer_1_out), .out_4(outA), .Load(or_1_out), .Clk(Clk));  // open: out_5
  not not_3 (not_3_out, or_3_out);
  Program_Counter program_counter_1 (
    .In(outA), .Inc(not_3_out), .Load(or_3_out), .Reset(Reset), .Clk(Clk),
    .out_6({program_counter_1_out_6[15], PC}));
  and and_9 (writeM, Insturction[3], Insturction[15]);
  Multiplexer #(.width(16), .enable("false")) multiplexer_2 (
    .in0(outA), .in1(InM), .out(multiplexer_2_out), .sel(Insturction[12]));
  ALU alu_1 (
    .x(outD), .y(multiplexer_2_out), .Output_8bits(outM), .zr(Zr), .ng(Ng), .zx(Insturction[11]),
    .zy(Insturction[9]), .nx(Insturction[10]), .ny(Insturction[8]), .f(Insturction[7]), .no(Insturction[6]));

  // Other names for the same wires on the sheet: ALU_out[15:0] = outM; ins0 = Insturction[0];
  //   Instruction[15:0] = Insturction; ins1 = Insturction[1]; ins2 = Insturction[2]; ins3 = Insturction[3];
  //   ins4 = Insturction[4]; ins5 = Insturction[5]; ins6 = Insturction[6]; ins7 = Insturction[7];
  //   ins8 = Insturction[8]; ins9 = Insturction[9]; ins10 = Insturction[10]; ins11 = Insturction[11];
  //   ins12 = Insturction[12]; ins13 = Insturction[13]; ins14 = Insturction[14]; ins15 = Insturction[15]

  // Notes on the sheet:
  //   Input
  //   Output
  //   A Regis
  //   D Regis
  //   PC
  //   ALU
endmodule
